# Fritzing sketch bmp180 (saved by Fritzing 0.9.3b)

parts:
  Part1 = Barometric Pressure Sensor - BMP180 Breakout (GY-68)
  MCU2 = Raspberry Pi Zero 2 W

nets:
  N1: Part1.VCC, MCU2.pin_1, MCU2.pin_17
  N2: Part1.GND, MCU2.pin_9, MCU2.pin_39
  N3: Part1.SCL, MCU2.pin_5
  N4: Part1.SDA, MCU2.pin_3

custom parts:
  Raspberry Pi Zero 2 W: The Raspberry Pi Zero is half the size of a Model A+, with twice the utility. A tiny Raspberry Pi that’s affordable enough for any project! · 1Ghz, Single-core CPU · 512MB RAM · Mini HDMI and USB On-The-Go ports · Micro USB power · HAT-compatible 40-pin header. Jan 2018: In this version schematic has been changed so the pins match the GPIO connector. I.e. the left hand pins are all the pins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
