# Fritzing sketch receiver (saved by Fritzing 0.9.3b)
breadboards: 1

parts:
  Mod2 = KY-022 Infrared Receiver Module [package="Breakout board"]
  Part1 = Arduino Nano (Rev3.0)
  LED1 = LED - 5mm [color="Red (633nm)" package="5 mm [THT]"]

nets:
  N1: Mod2.-, Part1.GND, LED1.cathode
  VIN: Mod2.Vin, Part1.5V
  N2: Mod2.S, Part1.D6
  N3: Part1.D13/SCK, LED1.anode

custom parts:
  KY-022 Infrared Receiver Module: KY-022 IR receiver module, reacts to 38kHz infrared light.
