# Fritzing sketch lidar (saved by Fritzing 0.9.3b)
breadboards: 1

parts:
  Mod1 = Raspberry Pi Pico W
  A1 = tf-luna lidar

nets:
  N1: Mod1.pin_3, Mod1.pin_8, Mod1.pin_13, Mod1.pin_18, Mod1.pin_23, Mod1.pin_28, Mod1.pin_33, Mod1.pin_38, A1.Pin_4
  N2: Mod1.pin_21, A1.Pin_2
  N3: Mod1.pin_22, A1.Pin_3
  N4: Mod1.pin_36, A1.Pin_1

custom parts:
  Raspberry Pi Pico W: Raspberry Pi Pico W. Based around the RP2040 microcontroller the Pico W is a low cost microcontroller device bringing Raspberry Pi quality, cost, and easy of use to the microcontroller space. The areas marked KEEPOUT in pcb silkscreen should not have traces running through them to avoid shorts on a soldered in module!
  tf-luna lidar: TF-Luna is using Time of Flight (TOF) principle to measure distance, and it periodically emits near infrared modulated wave.
