# Fritzing sketch motor (saved by Fritzing 0.9.3b)

parts:
  Mod1 = L298N DC motor driver
  M1 = DC Motor  # not connected
  VCC1 = Battery block 9V  # not connected
  MCU1 = Raspberry Pi Zero 2 W

nets:
  N1: Mod1.GND, MCU1.pin_6, MCU1.pin_39
  N2: Mod1.IN1, MCU1.pin_29
  N3: Mod1.IN2, MCU1.pin_31

notes:
  Common ground!

custom parts:
  L298N DC motor driver: 2x DC motor driver with 78M05 positive voltage regulator (7..35 V) L298N: max 46 V, 2 A Set 5 V Enable jumper to enable 5 V regultor (needed for the L298N) and +5 V output at screw terminal or supply external +5 V at screw terminal Set ENA and/or ENB to +5 V to enable motor permanently or supply ENA and/or ENB with PWM signal IN1 and IN2 set rotation directory for motor A (OUT1/OUT2) IN2 and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
  Raspberry Pi Zero 2 W: The Raspberry Pi Zero is half the size of a Model A+, with twice the utility. A tiny Raspberry Pi that’s affordable enough for any project! · 1Ghz, Single-core CPU · 512MB RAM · Mini HDMI and USB On-The-Go ports · Micro USB power · HAT-compatible 40-pin header. Jan 2018: In this version schematic has been changed so the pins match the GPIO connector. I.e. the left hand pins are all the pins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
