# Fritzing sketch rfid (saved by Fritzing 0.9.3b)
circuit board: 5.66858cm x 3.50556cm
breadboards: 1

parts:
  Mod1 = Raspberry Pi Pico W
  U1 = RFID RC522 SIP - 8 pins [chip_label="RFID RC522" package="SIP (Single Inline) [THT]"]

nets:
  N1: Mod1.pin_3, Mod1.pin_8, Mod1.pin_13, Mod1.pin_18, Mod1.pin_23, Mod1.pin_28, Mod1.pin_33, Mod1.pin_38, Mod1.pin_42, U1.GND
  N2: Mod1.pin_6, U1.MOSI
  N3: Mod1.pin_7, U1.IRQ
  N4: Mod1.pin_9, U1.NSS
  N5: Mod1.pin_10, U1.SCK
  N6: Mod1.pin_29, U1.RST
  N7: Mod1.pin_36, U1.VCC

custom parts:
  Raspberry Pi Pico W: Raspberry Pi Pico W. Based around the RP2040 microcontroller the Pico W is a low cost microcontroller device bringing Raspberry Pi quality, cost, and easy of use to the microcontroller space. The areas marked KEEPOUT in pcb silkscreen should not have traces running through them to avoid shorts on a soldered in module!
  RFID RC522 SIP - 8 pins: A SIP stand-in part for RFID RC522 . With 8 pins on a 300 mil single inline package (SIP) footprint.
