# Fritzing sketch tf-luna (saved by Fritzing 1.0.5)

parts:
  A1 = tf-luna lidar
  MCU1 = Raspberry Pi Zero 2 W

nets:
  N1: A1.Pin_1, MCU1.pin_2, MCU1.pin_4
  N2: A1.Pin_2, MCU1.pin_8
  N3: A1.Pin_3, MCU1.pin_10
  N4: A1.Pin_4, MCU1.pin_6, MCU1.pin_39

custom parts:
  tf-luna lidar: TF-Luna is using Time of Flight (TOF) principle to measure distance, and it periodically emits near infrared modulated wave.
  Raspberry Pi Zero 2 W: The Raspberry Pi Zero is half the size of a Model A+, with twice the utility. A tiny Raspberry Pi that’s affordable enough for any project! · 1Ghz, Single-core CPU · 512MB RAM · Mini HDMI and USB On-The-Go ports · Micro USB power · HAT-compatible 40-pin header. Jan 2018: In this version schematic has been changed so the pins match the GPIO connector. I.e. the left hand pins are all the pins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
