# Fritzing sketch thermometer (saved by Fritzing 0.9.3b)
breadboards: 1

parts:
  Mod1 = Raspberry Pi Pico W
  R1 = Resistor [tolerance=±5% resistance=4.7k package=THT]
  DS1 = DS18B20 1-Wire Temperature Sensor [part_number=DS18B20]

nets:
  N1: Mod1.pin_3, Mod1.pin_23
  N2: Mod1.pin_5, DS1.GND
  N3: Mod1.pin_17, Mod1.pin_39
  N4: Mod1.pin_19, Mod1.pin_22, Mod1.pin_32, R1.Pin_0, DS1.VDD
  N5: Mod1.pin_27, Mod1.pin_29, Mod1.pin_34
  N6: R1.Pin_1, DS1.DQ

custom parts:
  Raspberry Pi Pico W: Raspberry Pi Pico W. Based around the RP2040 microcontroller the Pico W is a low cost microcontroller device bringing Raspberry Pi quality, cost, and easy of use to the microcontroller space. The areas marked KEEPOUT in pcb silkscreen should not have traces running through them to avoid shorts on a soldered in module!
