# Fritzing sketch all_sensors (saved by Fritzing 0.9.3b)
breadboards: 1

parts:
  MCU1 = Raspberry Pi Zero 2 W
  Part1 = Barometric Pressure Sensor - BMP180 Breakout (GY-68)
  Part2 = InvenSense MPU6050
  A1 = tf-luna lidar
  Mod1 = L298N DC motor driver
  M1 = DC Motor
  VCC1 = Battery block 9V

nets:
  N1: MCU1.pin_1, MCU1.pin_17, Part1.VCC
  N2: MCU1.pin_2, MCU1.pin_4, Part2.VCC, A1.Pin_1
  N3: MCU1.pin_3, Part1.SDA, Part2.SDA
  N4: MCU1.pin_5, Part1.SCL, Part2.SCL
  GND: MCU1.pin_6, MCU1.pin_9, MCU1.pin_20, Part1.GND, Part2.GND, A1.Pin_4, Mod1.GND, VCC1.-
  N5: MCU1.pin_8, A1.Pin_2
  N6: MCU1.pin_10, A1.Pin_3
  N7: MCU1.pin_29, Mod1.IN2
  N8: MCU1.pin_31, Mod1.IN1
  N9: Mod1.OUT1, M1.pin_2
  N10: Mod1.OUT2, M1.pin_1
  N11: Mod1.12V, VCC1.+
  N12: Mod1.+5V-J1, Mod1.+5V-J2, Mod1.ENA, Mod1.ENB

custom parts:
  Raspberry Pi Zero 2 W: The Raspberry Pi Zero is half the size of a Model A+, with twice the utility. A tiny Raspberry Pi that’s affordable enough for any project! · 1Ghz, Single-core CPU · 512MB RAM · Mini HDMI and USB On-The-Go ports · Micro USB power · HAT-compatible 40-pin header. Jan 2018: In this version schematic has been changed so the pins match the GPIO connector. I.e. the left hand pins are all the pins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
  tf-luna lidar: TF-Luna is using Time of Flight (TOF) principle to measure distance, and it periodically emits near infrared modulated wave.
  L298N DC motor driver: 2x DC motor driver with 78M05 positive voltage regulator (7..35 V) L298N: max 46 V, 2 A Set 5 V Enable jumper to enable 5 V regultor (needed for the L298N) and +5 V output at screw terminal or supply external +5 V at screw terminal Set ENA and/or ENB to +5 V to enable motor permanently or supply ENA and/or ENB with PWM signal IN1 and IN2 set rotation directory for motor A (OUT1/OUT2) IN2 and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
